# Fritzing sketch tappo (saved by Fritzing 0.9.6b)
breadboards: 1

parts:
  J3 = STM32 Nucleo boards
  LED2 = LED - 5mm [color="Red (633nm)" package="5 mm [THT]"]
  S2 = Momentary Switch [package=ksa_sealed_tac_switch]
  R1 = Resistor [tolerance=±5% resistance=220 package="1206 [SMD]"]
  R2 = Resistor [tolerance=±5% resistance=220 package="1206 [SMD]"]
  J4 = Piezo Speaker
  HC-SR04_Sensor_3 = HC-SR04 Ultrasonic Distance Sensor

nets:
  N1: J3.D1/TX, S2.3
  N2: J3.D2, HC-SR04_Sensor_3.TRIG
  N3: J3.D3_PWM, HC-SR04_Sensor_3.ECHO
  N4: J3.D4, J4.pin2
  N5: J3.D5_PWM, LED2.anode
  5V: J3.5V, S2.2, HC-SR04_Sensor_3.VCC
  GND: J3.GND, R1.Pin_1, R2.Pin_1, J4.pin1, HC-SR04_Sensor_3.GND
  N6: LED2.cathode, R2.Pin_0
  N7: S2.4, R1.Pin_0
